# Fritzing sketch JR Gamepad Module Breadboard (saved by Fritzing 0.9.4)
breadboards: 1

parts:
  ESP32_D1_Mini = MH-ET Live Minikit for ESP32
  U1 = Voltage Regulator - 3.3V [package="TO220 [THT]"]
  J1 = female pin header, 5 pins [form="♀ (female)"]
  C1 = Electrolytic Capacitor [capacitance=10µF package="100 mil [THT, electrolytic]"]
  R1 = Resistor [tolerance=±5% resistance=44k package=THT]
  R2 = Resistor [tolerance=±5% resistance=330 package=THT]
  R3 = Resistor [tolerance=±5% resistance=14k package=THT]
  S1 = Toggle Switch [package=THT]
  Q1 = NPN-Transistor [package="TO92 [THT]"]

nets:
  N1: ESP32_D1_Mini.3.3V, U1.output_voltage, C1.+, R3.Pin_0
  N2: ESP32_D1_Mini.IO22, R3.Pin_1, Q1.C
  GND: ESP32_D1_Mini.GND, U1.GND, J1.pin2, C1.-, R2.Pin_0
  N3: U1.input_voltage, S1.L2
  N4: J1.pin3, S1.COM
  N5: J1.pin5, R1.Pin_0
  N6: R1.Pin_1, Q1.B
  N7: R2.Pin_1, Q1.E

notes:
  JR Module bay PIN mappings on Jumper brand transmitters:
  5 : PPM signal (3.3V)
  4 : nc
  3 : BATT (8V)
  2 : GND
  1 : nc
  ESP32 power supply:
  - The ON / OFF switch cuts power when the module is not being used
  - 3.3V linear regulator or step-down buck converter (preferred)
  - capacitor helps smoothing out Wifi/BT power spikes
  Transistor circuit for level-shifting the PPM input signal voltage to 3.3V:
  The PPM signal voltage is typically 3.3V, but it could also be 5V or something else!
  ESP32 D1 mini board:
  Can be a different ESP32 board, but it will have to fit in the JR module enclosure along with the other components.

custom parts:
  MH-ET Live Minikit for ESP32: MH-ET Live Minikit for ESP32 ( http://mh.nodebb.com/topic/8/mh-et-live-minikit-for-esp32/2/) PCB footprint is invalid.
