# Fritzing sketch JR Gamepad Module Stripboard (saved by Fritzing 0.9.4)
stripboards: 1

parts:
  ESP32_D1_Mini = MH-ET Live Minikit for ESP32
  U1 = Voltage Regulator - 3.3V [package="TO220 [THT]"]
  J1 = female pin header, 5 pins [form="♀ (female)"]
  C1 = Electrolytic Capacitor [capacitance=10µF package="100 mil [THT, electrolytic]"]
  R1 = Resistor [tolerance=±5% resistance=47k package=THT]
  R2 = Resistor [tolerance=±5% resistance=330 package=THT]
  S1 = Toggle Switch [package=THT]
  R3 = Resistor [tolerance=±5% resistance=15k package=THT]
  Q1 = NPN-Transistor [part_number=BC547 package="TO92 [THT]"]

nets:
  N1: ESP32_D1_Mini.3.3V, U1.output_voltage, C1.+, R3.Pin_0
  N2: ESP32_D1_Mini.IO22, R3.Pin_1, Q1.C
  GND: ESP32_D1_Mini.GND, U1.GND, J1.pin2, C1.-, R2.Pin_0
  N3: U1.input_voltage, S1.L2
  N4: J1.pin3, S1.COM
  N5: J1.pin5, R1.Pin_0
  N6: R1.Pin_1, Q1.B
  N7: R2.Pin_1, Q1.E

notes:
  Notes:
  - This stripboard layout fits the "DIY box" found in Jumper transmitters
  - Use the "Layers" window to hide the parts & wires / to only see the board, as there are quite a few strips to be cut.
  - The JR module bay has 5 long protruding pins, requiring to dremel/cut the lower left corner of the stripboard, then fitting something like a Molex 22-14-2054 board connector for proper interfacing.
  But a simple, straight 5-pin female header will work just as well:
  - Fit the stripboard into the module case, screw the board into place, and put the module in the transmitter.
  Check if everything fits and ensure that there's about 2mm clearance around the module bay pins.
  - Take a 5-pin female header, bend its pins 180° around and plug it carefully onto the transmitter's pins, while adjusting/bending the header pins until they align perfectly with the stripboard sockets.
  - With everything in place, solder the header pins to the stripboard.
  Finally, adding a dab of epoxy will ensure the header stays solidly attached to the stripboard.
  - The 3.3V regulator will not fit on top. Mount it to the back of the board.
  - Check your particular transistor's pin layout! The stripboard assumes the following layout from bottom to top: Emitter, Base, Collector. Don't twist a BC547's legs as depicted, simply rotate the transistor 180°!
  - Unused strips are grounded on purpose to make the board act as a ground plane. Join adjacent stripes with blobs of solder.
  - The on/off switch is meant to be fitted to the module's plastic cover
  - You will have to do a cutout in the DIY box if you want to plug a cable into the ESP32's USB port without disassembling the module.
  This means the USB port cannot be used while the module is fitted in the transmitter. And that's actually a good thing, because powering the board with both the transmitter and USB could lead to a puff of smoke in any of the involved parties ;-)

custom parts:
  MH-ET Live Minikit for ESP32: MH-ET Live Minikit for ESP32 ( http://mh.nodebb.com/topic/8/mh-et-live-minikit-for-esp32/2/) PCB footprint is invalid.
